// Logisim project 6651071061_LAB1_Bai1trang4.circ as structural Verilog: 1 circuit, main circuit main
module main (
  input  A2,
  input  A1,
  input  A0,
  input  EN,
  output Y0,
  output Y1,
  output Y2,
  output Y3,
  output Y4,
  output Y5,
  output Y6,
  output Y7
);

  wire not_1_out, not_2_out, not_3_out;

  not not_1 (not_1_out, A2);
  not not_2 (not_2_out, A1);
  not not_3 (not_3_out, A0);
  and and_1 (Y0, not_1_out, not_2_out, not_3_out, EN);
  and and_2 (Y1, not_1_out, not_2_out, not_3_out, EN);
  and and_3 (Y2, not_1_out, not_2_out, not_3_out, EN);
  and and_4 (Y3, not_1_out, not_2_out, not_3_out, EN);
  and and_5 (Y4, not_1_out, not_2_out, not_3_out, EN);
  and and_6 (Y5, not_1_out, not_2_out, not_3_out, EN);
  and and_7 (Y6, not_1_out, not_2_out, not_3_out, EN);
  and and_8 (Y7, not_1_out, not_2_out, not_3_out, EN);

  // Notes on the sheet:
  //   Lê Đình Sơn - 6651071061
endmodule
