// Logisim project 6651071061_LAB1_Bai3trang5.circ as structural Verilog: 2 circuits, main circuit main
module main (
  input  [3:0] A,
  input  [3:0] B,
  output [3:0] sum,
  output cout
);

  wire FA_0_cout, FA_1_cout, FA_2_cout;

  FA FA_0 (.A(A[0]), .B(B[0]), .Cin(1'b0), .Sum(sum[0]), .Cout(FA_0_cout));
  FA FA_1 (.A(A[1]), .B(B[1]), .Cin(FA_0_cout), .Sum(sum[1]), .Cout(FA_1_cout));
  FA FA_2 (.A(A[2]), .B(B[2]), .Cin(FA_1_cout), .Sum(sum[2]), .Cout(FA_2_cout));
  FA FA_3 (.A(A[3]), .B(B[3]), .Cin(FA_2_cout), .Sum(sum[3]), .Cout(cout));

  // Notes on the sheet:
  //   Lê ĐÌnh Sơn - 6651071061
endmodule

module FA (
  input  A,
  input  B,
  input  Cin,
  output Sum,
  output Cout
);

  wire and_1_out, and_2_out, xor_1_out;

  xor xor_1 (xor_1_out, A, B);
  and and_1 (and_1_out, A, B);
  xor xor_2 (Sum, xor_1_out, Cin);
  and and_2 (and_2_out, Cin, xor_1_out);
  or or_1 (Cout, and_2_out, and_1_out);

  // Notes on the sheet:
  //   Lê ĐÌnh Sơn - 6651071061
endmodule
