// Logisim project 6651071061_LAB1_Bai5trang6.circ as structural Verilog: 1 circuit, main circuit main
module main (
  input  A3,
  input  A2,
  input  A1,
  input  A0,
  input  B3,
  input  B2,
  input  B1,
  input  B0,
  output A_B,
  output A_B_2,
  output A_B_3
);

  wire and_2_out, and_3_out, and_4_out, comparator_1_eq, comparator_1_gt, comparator_2_eq, comparator_2_gt,
       comparator_3_eq, comparator_3_gt, comparator_4_eq, comparator_4_gt;

  Comparator #(.width(1), .mode("unsigned")) comparator_1 (
    .a(A3), .b(B3), .gt(comparator_1_gt), .eq(comparator_1_eq));  // open: lt
  Comparator #(.width(1), .mode("unsigned")) comparator_2 (
    .a(A2), .b(B2), .gt(comparator_2_gt), .eq(comparator_2_eq));  // open: lt
  Comparator #(.width(1), .mode("unsigned")) comparator_3 (
    .a(A1), .b(B1), .gt(comparator_3_gt), .eq(comparator_3_eq));  // open: lt
  Comparator #(.width(1), .mode("unsigned")) comparator_4 (
    .a(A0), .b(B0), .gt(comparator_4_gt), .eq(comparator_4_eq));  // open: lt
  and and_1 (A_B, comparator_1_eq, comparator_2_eq, comparator_3_eq, comparator_4_eq);
  and and_2 (and_2_out, comparator_1_eq, comparator_2_gt);
  and and_3 (and_3_out, comparator_1_eq, comparator_2_eq, comparator_3_gt);
  and and_4 (and_4_out, comparator_1_eq, comparator_2_eq, comparator_3_eq, comparator_4_gt);
  or or_1 (A_B_3, comparator_1_gt, and_2_out, and_3_out, and_4_out);
  nor nor_1 (A_B_2, A_B, A_B_3);

  // Notes on the sheet:
  //   Lê Đình Sơn - 6651071061
endmodule
